// Logisim project DLD Lab 2.circ as structural Verilog: 1 circuit, main circuit main
module main (
  input  [6:0] A,
  input  [6:0] B,
  output [6:0] C
);

  assign C = A & B;  // AND_Gate AND, 7 bits wide

  // Notes on the sheet:
  //      C=A.B
endmodule
