// Logisim project FASU.circ as structural Verilog: 1 circuit, main circuit main
module main (
  input  NAND_GATE,
  input  NOT_GATE,
  input  NOR_GATE,
  input  in_4,
  input  in_5,
  input  in_6,
  input  in_7,
  input  OR_GATE,
  input  XOR_GATE,
  input  in_10,
  input  in_11,
  output out_12,
  output out_13,
  output out_14,
  output out_15,
  output out_16,
  output out_17
);

  not NOT (out_12, NOT_GATE);
  and AND_GATE (out_15, in_5, in_7);
  or u_OR_GATE (out_16, OR_GATE, in_10);
  nand NAND (out_13, NAND_GATE, NOR_GATE);
  nor NOR (out_14, in_4, in_6);
  xor XOR (out_17, XOR_GATE, in_11);

  // Notes on the sheet:
  //   AND GATE
endmodule
